# Fritzing sketch fritzing_wlan_Scheinwerfer (saved by Fritzing 0.9.3b)

parts:
  U1 = ESP32S-HiLetgo [part_number=ESP32S-HiLetgo]
  HLK-PM1 = HLK-PM01
  KY-1 = Keyes Relay [package=THT]
  BULB1 = Incandescent light bulb small [package="bulb sm"]
  J1 = Camdenboss CTB0158-2 [part_number=CTB0158-2 package=THT]
  J2 = Camdenboss CTB0158-2 [part_number=CTB0158-2 package=THT]

nets:
  N1: U1.3.3, KY-1.power
  N2: U1.GPIO36, KY-1.signal
  N3: U1.VIN, HLK-PM1.+Vo
  N4: U1.GND, KY-1.ground
  N5: HLK-PM1.AC#0, KY-1.C, J2.terminal_2
  N6: HLK-PM1.AC#1, BULB1.1, J1.pin1
  N7: KY-1.NO, BULB1.2

custom parts:
  ESP32S-HiLetgo: HiLetgo ESP-WROOM-32 ESP32 ESP-32S Development Board 2.4GHz Dual-Mode WiFi + Bluetooth Dual Cores Microcontroller The ESP32 integrated with Antenna switches, RF Balun, power amplifiers, low-noise amplifiers, filters, and management modules, and the entire solution occupies the least area of PCB. 2.4 GHz Wi-Fi plus Bluetooth dual-mode chip, with TSMC Ultra-low power consumption 40nm technology,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
  Keyes Relay: The Keyes 5V relay module is suitable for SCM development, home appliance control. It uses a 5V~12V TIL control signal which can control DC / AC signal.
